# Fritzing sketch wiring (saved by Fritzing 0.9.3b)

parts:
  Raspberry_Pi_1 = Raspberry Pi 3 [part_number=RPI-3-V1.2]
  Part1 = USB converter CP2102

nets:
  N1: Raspberry_Pi_1.GIPO15, Part1.TXO
  N2: Raspberry_Pi_1.GIPO14, Part1.RXI
  GND: Raspberry_Pi_1.GND, Part1.GND
