# Fritzing sketch wiring_jtag (saved by Fritzing 0.9.3b)

parts:
  Raspberry_Pi_1 = Raspberry Pi 3 [part_number=RPI-3-V1.2]
  J1 = shrouded pin header, 20 pins [form="♂ (shrouded male)"]

nets:
  N1: Raspberry_Pi_1.3v3, J1.pin1
  N2: Raspberry_Pi_1.GND, J1.pin19
  N3: Raspberry_Pi_1.GIPO27, J1.pin4
  N4: Raspberry_Pi_1.GIPO22, J1.pin2
  N5: Raspberry_Pi_1.GIPO26, J1.pin3
  N6: Raspberry_Pi_1.GIPO25, J1.pin5
  N7: Raspberry_Pi_1.GIPO24, J1.pin7
  N8: Raspberry_Pi_1.GIPO23, J1.pin6
